// Digital circuit 02_04.dig as structural Verilog
module _02_04 (
  input  A,
  input  B,
  input  Cin,
  output Sum,
  output Cout
);

  wire a_t, b_t, c, or_1_out, or_2_out, or_3_out, or_4_out, or_5_out, or_6_out, or_7_out;

  or or_1 (or_1_out, a_t, B, c);
  or or_2 (or_2_out, a_t, b_t, Cin);
  or or_3 (or_3_out, A, b_t, c);
  or or_4 (or_4_out, A, B, Cin);
  and and_1 (Sum, or_1_out, or_2_out, or_3_out, or_4_out);
  not not_1 (a_t, A);
  not not_2 (b_t, B);
  not not_3 (c, Cin);
  or or_5 (or_5_out, A, B);
  or or_6 (or_6_out, A, Cin);
  or or_7 (or_7_out, B, Cin);
  and and_2 (Cout, or_5_out, or_6_out, or_7_out);

  // Other names for the same wires on the sheet: c_t = Cin
endmodule
