// Digital circuit 02_05.dig as structural Verilog
module _02_05 (
  input  A,
  input  B,
  input  C,
  input  D,
  output Z1,
  output Z2,
  output Z3
);

  wire a_t, and_1_out, and_2_out, and_3_out, and_4_out, and_5_out, and_6_out, and_7_out, and_8_out,
       and_9_out, and_10_out, b_t, c_t, d_t;

  and and_1 (and_1_out, A, c_t);
  and and_2 (and_2_out, d_t, B, c_t);
  and and_3 (and_3_out, A, B, d_t);
  and and_4 (and_4_out, a_t, b_t, c_t, d_t);
  and and_5 (and_5_out, a_t, B, c_t, D);
  and and_6 (and_6_out, A, B, C, D);
  and and_7 (and_7_out, A, b_t, C, d_t);
  not not_1 (a_t, A);
  not not_2 (b_t, B);
  or or_1 (Z1, and_1_out, and_2_out, and_3_out);
  or or_2 (Z3, and_4_out, and_5_out, and_6_out, and_7_out);
  not not_3 (c_t, C);
  and and_8 (and_8_out, a_t, C);
  and and_9 (and_9_out, b_t, C, D);
  and and_10 (and_10_out, a_t, b_t, D);
  not not_4 (d_t, D);
  or or_3 (Z2, and_8_out, and_9_out, and_10_out);
endmodule
