// Digital circuit 02_06.dig as structural Verilog
module _02_06 (
  input  A,
  input  B,
  input  C,
  input  D,
  output Z1,
  output Z2,
  output Z3
);

  wire a_t, b_t, c_t, d_t, or_1_out, or_2_out, or_3_out, or_4_out, or_5_out, or_6_out, or_7_out, or_8_out,
       or_9_out, or_10_out, or_11_out, or_12_out, or_13_out, or_14_out;

  or or_1 (or_1_out, A, B);
  or or_2 (or_2_out, A, c_t);
  or or_3 (or_3_out, A, d_t);
  or or_4 (or_4_out, c_t, d_t);
  or or_5 (or_5_out, c_t, a_t, B);
  and and_1 (Z1, or_1_out, or_2_out, or_3_out, or_4_out, or_5_out);
  not not_1 (a_t, A);
  not not_2 (b_t, B);
  not not_3 (c_t, C);
  or or_6 (or_6_out, C, D);
  or or_7 (or_7_out, a_t, C);
  or or_8 (or_8_out, b_t, C);
  or or_9 (or_9_out, a_t, b_t);
  or or_10 (or_10_out, a_t, c_t, D);
  not not_4 (d_t, D);
  and and_2 (Z2, or_6_out, or_7_out, or_8_out, or_9_out, or_10_out);
  or or_11 (or_11_out, A, c_t);
  or or_12 (or_12_out, a_t, C);
  or or_13 (or_13_out, b_t, D);
  or or_14 (or_14_out, B, d_t);
  and and_3 (Z3, or_11_out, or_12_out, or_13_out, or_14_out);
endmodule
