// Digital circuit 02_07.dig as structural Verilog
module _02_07 (
  input  X1,
  input  X0,
  input  Selector,
  output Z
);

  wire a, and_1_out, and_2_out, b, c;

  and and_1 (and_1_out, X0, c);
  and and_2 (and_2_out, X1, Selector);
  or or_1 (Z, and_1_out, and_2_out);
  not not_1 (a, X0);
  not not_2 (b, X1);
  not not_3 (c, Selector);

  // Other names for the same wires on the sheet: a_t = X0; b_t = X1; c_t = Selector
endmodule
