// Digital circuit 02_08.dig as structural Verilog
module _02_08 (
  input  X1,
  input  X0,
  input  Selector,
  output Z
);

  wire a, b, c, or_1_out, or_2_out;

  or or_1 (or_1_out, X0, Selector);
  or or_2 (or_2_out, X1, c);
  and and_1 (Z, or_1_out, or_2_out);
  not not_1 (a, X0);
  not not_2 (b, X1);
  not not_3 (c, Selector);

  // Other names for the same wires on the sheet: a_t = X0; b_t = X1; c_t = Selector
endmodule
