// Digital circuit 02_09.dig as structural Verilog
module _02_09 (
  input  X0,
  input  X1,
  input  X2,
  input  X3,
  input  S0,
  input  S1,
  output Z
);

  wire a, and_1_out, and_2_out, and_3_out, and_4_out, b, c, d, s0_t, s1_t;

  and and_1 (and_1_out, X0, s0_t, s1_t);
  and and_2 (and_2_out, X1, S0, s1_t);
  and and_3 (and_3_out, X2, s0_t, S1);
  and and_4 (and_4_out, X3, S0, S1);
  not not_1 (a, X0);
  not not_2 (b, X1);
  or or_1 (Z, and_1_out, and_2_out, and_3_out, and_4_out);
  not not_3 (c, X2);
  not not_4 (d, X3);
  not not_5 (s0_t, S0);
  not not_6 (s1_t, S1);

  // Other names for the same wires on the sheet: a_t = X0; b_t = X1; c_t = X2; d_t = X3
endmodule
