// Digital circuit 02_3.dig as structural Verilog
module _02_3 (
  input  A,
  input  B,
  input  Cin,
  output Sum,
  output Cout
);

  wire a_prime, and_1_out, and_2_out, and_3_out, and_4_out, and_5_out, and_6_out, and_7_out, and_8_out,
       b_prime, c_prime;

  not not_1 (a_prime, A);
  and and_1 (and_1_out, a_prime, b_prime, Cin);
  and and_2 (and_2_out, a_prime, B, c_prime);
  and and_3 (and_3_out, A, b_prime, c_prime);
  and and_4 (and_4_out, A, B, Cin);
  not not_2 (b_prime, B);
  not not_3 (c_prime, Cin);
  or or_1 (Sum, and_1_out, and_2_out, and_3_out, and_4_out);
  and and_5 (and_5_out, a_prime, B, Cin);
  and and_6 (and_6_out, A, b_prime, Cin);
  and and_7 (and_7_out, A, B, c_prime);
  and and_8 (and_8_out, A, B, Cin);
  or or_2 (Cout, and_5_out, and_6_out, and_7_out, and_8_out);

  // Other names for the same wires on the sheet: c = Cin
endmodule
