// Digital circuit 03_02.dig as structural Verilog
module _03_02 (
  input  [2:0] In,
  output [7:0] Z
);

  Multiplexer #(.Bits(8), .Selector_Bits(3)) multiplexer_1 (
    .sel(In), .in_0(8'h44), .in_1(8'h69), .in_2(8'h67), .in_3(8'h4c), .in_4(8'h6f), .in_5(8'h4c),
    .in_6(8'h61), .in_7(8'h62), .out(Z));
endmodule
