// Digital circuit 03_03.dig as structural Verilog
module _03_03 (
  input  [3:0] In,
  input  [1:0] Selector,
  output [3:0] Output
);

  wire [3:0] C, C1, C2, E;

  ROM #(.AddrBits(4), .Bits(4)) rom_1 (.A(In), .sel(1'b1), .D(E));
  ROM #(.AddrBits(4), .Bits(4)) rom_2 (.A(In), .sel(1'b1), .D(C));
  Multiplexer #(.Bits(4), .Selector_Bits(2)) multiplexer_1 (
    .sel(Selector), .in_0(E), .in_1(C), .in_2(C1), .in_3(C2), .out(Output));
  ROM #(.AddrBits(4), .Bits(4)) rom_3 (.A(In), .sel(1'b1), .D(C1));
  ROM #(.AddrBits(4), .Bits(4)) rom_4 (.A(In), .sel(1'b1), .D(C2));

  // Notes on the sheet:
  //   contents of rom_1 (hex, n*v repeats v):
  //   3,4,5,6,7,8,9,a,b,c
  //   contents of rom_2 (hex, n*v repeats v):
  //   0,1,3,2,6,7,5,4,c,d
  //   contents of rom_3 (hex, n*v repeats v):
  //   0,1,2,3,4,b,c,d,e,f
  //   contents of rom_4 (hex, n*v repeats v):
  //   0,5,2,9,4,b,6,d,a,f
endmodule
