// Digital circuit 03_04.dig as structural Verilog
module _03_04 (
  input  [6:0] In,
  output [6:0] Output
);

  wire a, b, c, d, e, f, g, s1, s2, s3;

  xor xor_1 (s3, In[3], In[2], In[1], In[0]);
  xor xor_2 (s2, In[5], In[4], In[1], In[0]);
  xor xor_3 (s1, In[6], In[4], In[2], In[0]);
  Decoder #(.Selector_Bits(3)) decoder_1 (
    .sel({s3, s2, s1}), .out_1(a), .out_2(b), .out_3(c), .out_4(d), .out_5(e), .out_6(f), .out_7(g));  // open: out_0
  xor xor_4 (Output[6], a, In[6]);
  xor xor_5 (Output[5], b, In[5]);
  xor xor_6 (Output[4], c, In[4]);
  xor xor_7 (Output[3], d, In[3]);
  xor xor_8 (Output[2], e, In[2]);
  xor xor_9 (Output[1], f, In[1]);
  xor xor_10 (Output[0], g, In[0]);

  // Other names for the same wires on the sheet: m4 = In[0]; m3 = In[1]; m2 = In[2]; p3 = In[3]; m1 = In[4];
  //   p2 = In[5]; p1 = In[6]
endmodule
