// Digital circuit 07_01.dig as structural Verilog
module _07_01 (
  input  clk,
  input  reset,
  input  C_2,
  input  B_2,
  input  A_2,
  output C,
  output B,
  output A,
  output C_plus,
  output B_plus,
  output A_plus
);

  wire and_1_out, and_2_out, and_3_out, and_4_out, and_5_out, and_6_out, and_7_out, not_1_out, not_2_out,
       not_3_out, or_1_out;

  and and_1 (and_1_out, ~reset, A);  // And
  D_FF d_ff_1 (.D(and_1_out), .C(clk), .Q(C));  // open: nQ
  and and_2 (and_2_out, ~reset, or_1_out);  // And
  or or_1 (or_1_out, ~B, and_3_out);  // Or
  and and_3 (and_3_out, ~A, ~C);  // And
  D_FF d_ff_2 (.D(and_2_out), .C(clk), .Q(B));  // open: nQ
  and and_4 (and_4_out, ~reset, and_5_out);  // And
  and and_5 (and_5_out, B, ~C);  // And
  D_FF d_ff_3 (.D(and_4_out), .C(clk), .Q(A));  // open: nQ
  not not_1 (not_1_out, C_2);
  not not_2 (not_2_out, B_2);
  not not_3 (not_3_out, A_2);
  and and_6 (and_6_out, not_3_out, not_1_out);
  and and_7 (and_7_out, B_2, not_1_out);
  or or_2 (B_plus, and_6_out, not_2_out);
  or or_3 (A_plus, A_2, and_7_out);

  assign C_plus = A_2;
endmodule
