// Digital circuit Quiz1.dig as structural Verilog
module Quiz1 (
  input  [3:0] in,
  output out
);

  wire and_1_out, and_2_out, and_3_out, and_4_out;

  and and_1 (and_1_out, in[0], ~in[1]);  // And
  and and_2 (and_2_out, in[3], in[1], ~in[0]);  // And
  and and_3 (and_3_out, in[2], ~in[3], ~in[1]);  // And
  and and_4 (and_4_out, in[0], ~in[3], ~in[2]);  // And
  or or_1 (out, and_1_out, and_2_out, and_3_out, and_4_out);

  // Other names for the same wires on the sheet: D = in[0]; C = in[1]; B = in[2]; A = in[3]
endmodule
