// Digital circuit Quiz2.dig as structural Verilog
module Quiz2 (
  input  [3:0] in0,
  input  [3:0] in1,
  input  addsubtract,
  output [2:0] out
);

  wire [2:0] A, D, z, z1;

  BitCount #(.Bits(4)) bitcount_1 (.in(in0), .out(A));
  BitCount #(.Bits(4)) bitcount_2 (.in(in1), .out(D));
  Multiplexer #(.Bits(3)) multiplexer_1 (.sel(addsubtract), .in_0(z), .in_1(z1), .out(out));
  Add #(.Bits(3)) add_1 (.a(A), .b(D), .c_i(1'b0), .s(z));  // open: c_o
  Sub #(.Bits(3)) sub_1 (.a(A), .b(D), .c_i(1'b0), .s(z1));  // open: c_o
endmodule
