// Digital circuit exam11.dig as structural Verilog
module exam11 (
  input  X1,
  input  X2,
  input  X3,
  input  X4,
  output Y1
);

  wire and_1_out, and_2_out, and_3_out, not_2_out, not_3_out;

  // Not not_1 has open pins: in=X2, out=open
  not not_2 (not_2_out, X3);
  not not_3 (not_3_out, X4);
  and and_1 (and_1_out, X1, not_2_out);
  and and_2 (and_2_out, X2, X3, X4);
  and and_3 (and_3_out, X1, X2, X4);
  or or_1 (Y1, and_1_out, and_2_out, and_3_out);
endmodule
